# Fritzing sketch stm32-drum (saved by Fritzing 0.9.3b)
breadboards: 2

parts:
  Part1 = Arduino Nano (Rev3.0)  # not connected
  U1 = STM32F103C8T6 blue mini board  # not connected
  Grove1 = Grove OLED 128x96  # not connected
  Part2 = FTDI Basic Programmer
  R1 = Resistor [tolerance=±5% resistance=220 package="0603 [SMD]"]
  C1 = Capacitor [package=cap-pth-5mm]
  U3 = AUDIO-JACK2 [package=audio-jack]
  S1 = Pushbutton [package="[THT]"]
  S2 = Pushbutton [package="[THT]"]
  LED1 = LED - 5mm [color="Red (633nm)" package="5 mm [THT]"]
  R2 = Resistor [tolerance=±5% resistance=220 package="0603 [SMD]"]

nets:
  N1: Part2.GND, R2.Pin_1
  N2: R1.Pin_0, U3.TIP
  N3: R1.Pin_1, C1.2
  N4: C1.1, U3.SLEEVE, S1.Pin_1, S1.Pin_2, S2.Pin_1, S2.Pin_2
  N5: S1.Pin_3, S1.Pin_4
  N6: S2.Pin_3, S2.Pin_4
  N7: LED1.cathode, R2.Pin_0

notes:
  FTDI
  3.5mm audio OUT
  1.3" OLED I2C screen
  PLAY
  RECORD
